# Fritzing sketch Diagrama (saved by Fritzing 0.9.3b)
breadboards: 1

parts:
  Componente1 = Arduino Uno (Rev3)
  LED1 = LED - 5mm [color="Red (633nm)" package="5 mm [THT]"]
  R1 = Resistor [tolerance=±5% resistance=220 package=THT]
  R2 = Rotary Potentiometer (Small) [maximum_resistance=100kΩ package=THT]
  R3 = Resistor [tolerance=±5% resistance=220 package=THT]
  LED2 = LED - 5mm [color="Red (633nm)" package="5 mm [THT]"]
  R4 = Resistor [tolerance=±5% resistance=220 package=THT]
  LED3 = LED - 5mm [color="Red (633nm)" package="5 mm [THT]"]
  R5 = Resistor [tolerance=±5% resistance=220 package=THT]
  LED4 = LED - 5mm [color="Red (633nm)" package="5 mm [THT]"]
  R6 = Resistor [tolerance=±5% resistance=220 package=THT]
  LED5 = LED - 5mm [color="Red (633nm)" package="5 mm [THT]"]

nets:
  N1: Componente1.A0, R2.wiper
  N2: Componente1.D3_PWM, LED1.anode
  N3: Componente1.D4, LED2.anode
  N4: Componente1.D5_PWM, LED3.anode
  N5: Componente1.D6_PWM, LED4.anode
  N6: Componente1.D7, LED5.anode
  N7: Componente1.5V, R2.leg1
  N8: Componente1.GND, R2.leg2
  N9: LED1.cathode, R1.Pin_1
  N10: R3.Pin_1, LED2.cathode
  N11: R4.Pin_1, LED3.cathode
  N12: R5.Pin_1, LED4.cathode
  N13: R6.Pin_1, LED5.cathode
